# Fritzing sketch KitchenEnvMonitorSystem (saved by Fritzing 0.9.8b)

parts:
  U2 = NodeMCU V3.0
  J1 = SSD1306 128x64 1.3Inch [form="♂ (male)" package=THT]
  J2 = BH1750 [form="♂ (male)" package=THT]
  KY-1 = Keyes Relay [package=THT]
  KY-2 = Keyes Relay [package=THT]
  J3 = HC-SR501 [form="♀ (female)" package=THT]
  J4 = DHT11 basic temperature-humidity sensor [form="♂ (male)" package=THT]
  A1 = MH-FMD buzzer
  S1 = KY-026
  LED1 = RGB LED - (4 legs) [package="5 mm [THT]"]
  元件1 = MQ-4
  R2 = Resistor [tolerance=±5% resistance=220 package="0402 [SMD]"]
  R1 = Resistor [tolerance=±5% resistance=220 package="0402 [SMD]"]

nets:
  N1: U2.D0, KY-2.signal
  N2: U2.D1, KY-1.ground
  N3: U2.D2, J1.SDA, J2.SDA
  N4: U2.D3, J1.SCL, J2.SCL
  N5: U2.D4, A1.Pin_2
  VCC: U2.3V3, J1.VCC, J2.VCC, KY-1.power, KY-2.power, J3.VCC, J4.VCC, A1.Pin_1, S1.pin3
  GND: U2.GND, J1.GND, J2.GND, KY-1.signal, KY-2.ground, J3.GND, J4.GND, A1.Pin_3, S1.pin2, LED1.common_anode
  N6: U2.D5, J3.SIG
  N7: U2.D6, J4.OUT
  N8: U2.D7, S1.pin4
  N9: U2.D8, LED1.red_cathode
  N10: U2.RSV#40, 元件1.VCC
  N11: U2.RSV#41, 元件1.GND, R2.Pin_0
  N12: U2.A0, R2.Pin_1, R1.Pin_0
  N13: 元件1.DO, R1.Pin_1

custom parts:
  NodeMCU V3.0: NodeMcu V3 Lua WIFI Development Board
  SSD1306 128x64 1.3Inch: These displays are small, only about 1" diagonal, but very readable due to the high contrast of an OLED display. This display is made of 128x64 individual white OLED pixels, each one is turned on or off by the controller chip. Because the display makes its own light, no backlight is required. This reduces the power required to run the OLED and is why the display has such high contrast; we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
  BH1750: BH1750FVI is an digital Ambient Light Sensor IC for I2 C bus interface. This IC is the most suitable to obtain the ambient light data for adjusting LCD and Keypad backlight power of Mobile phone. It is possible to detect wide range at High resolution.
  Keyes Relay: The Keyes 5V relay module is suitable for SCM development, home appliance control. It uses a 5V~12V TIL control signal which can control DC / AC signal.
  DHT11 basic temperature-humidity sensor: The DHT11 is a basic, ultra low-cost digital temperature and humidity sensor. It uses a capacitive humidity sensor and a thermistor to measure the surrounding air, and spits out a digital signal on the data pin (no analog input pins needed). Its fairly simple to use, but requires careful timing to grab data. The only real downside of this sensor is you can only get new data from it once every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
  MH-FMD buzzer: MH-FMD buzzer.
  KY-026: ky-026 flame sensor module
